// Logisim project hw.circ as structural Verilog
module register (
  input  [15:0] rIn,
  input  Reset,
  input  wEnable,
  output [15:0] rOut
);

  wire clk;
  wire [15:0] and_1_out, multiplexer_1_out, multiplexer_2_out;

  Clock clock_1 (.out(clk));
  D_Flip_Flop d_ff_1 (.clk(clk), .D(multiplexer_2_out[15]), .Q(rOut[15]));  // open: Qn, preset, en, reset
  D_Flip_Flop d_ff_2 (.clk(clk), .D(multiplexer_2_out[14]), .Q(rOut[14]));  // open: Qn, preset, en, reset
  D_Flip_Flop d_ff_3 (.clk(clk), .D(multiplexer_2_out[13]), .Q(rOut[13]));  // open: Qn, preset, en, reset
  D_Flip_Flop d_ff_4 (.clk(clk), .D(multiplexer_2_out[12]), .Q(rOut[12]));  // open: Qn, preset, en, reset
  assign and_1_out = rIn & {16{1'b0}};  // AND_Gate and_1, 16 bits wide
  D_Flip_Flop d_ff_5 (.clk(clk), .D(multiplexer_2_out[11]), .Q(rOut[11]));  // open: Qn, preset, en, reset
  Multiplexer #(.width(16)) multiplexer_1 (
    .in0(rIn), .in1(and_1_out), .out(multiplexer_1_out), .sel(Reset));  // open: en
  D_Flip_Flop d_ff_6 (.clk(clk), .D(multiplexer_2_out[10]), .Q(rOut[10]));  // open: Qn, preset, en, reset
  D_Flip_Flop d_ff_7 (.clk(clk), .D(multiplexer_2_out[9]), .Q(rOut[9]));  // open: Qn, preset, en, reset
  Multiplexer #(.width(16)) multiplexer_2 (
    .in0(rOut), .in1(multiplexer_1_out), .out(multiplexer_2_out), .sel(wEnable));  // open: en
  D_Flip_Flop d_ff_8 (.clk(clk), .D(multiplexer_2_out[8]), .Q(rOut[8]));  // open: Qn, preset, en, reset
  D_Flip_Flop d_ff_9 (.clk(clk), .D(multiplexer_2_out[7]), .Q(rOut[7]));  // open: Qn, preset, en, reset
  D_Flip_Flop d_ff_10 (.clk(clk), .D(multiplexer_2_out[6]), .Q(rOut[6]));  // open: Qn, preset, en, reset
  D_Flip_Flop d_ff_11 (.clk(clk), .D(multiplexer_2_out[5]), .Q(rOut[5]));  // open: Qn, preset, en, reset
  D_Flip_Flop d_ff_12 (.clk(clk), .D(multiplexer_2_out[4]), .Q(rOut[4]));  // open: Qn, preset, en, reset
  D_Flip_Flop d_ff_13 (.clk(clk), .D(multiplexer_2_out[3]), .Q(rOut[3]));  // open: Qn, preset, en, reset
  D_Flip_Flop d_ff_14 (.clk(clk), .D(multiplexer_2_out[2]), .Q(rOut[2]));  // open: Qn, preset, en, reset
  D_Flip_Flop d_ff_15 (.clk(clk), .D(multiplexer_2_out[1]), .Q(rOut[1]));  // open: Qn, preset, en, reset
  D_Flip_Flop d_ff_16 (.clk(clk), .D(multiplexer_2_out[0]), .Q(rOut[0]));  // open: Qn, preset, en, reset

  // Other names for the same wires on the sheet: ot[15:0] = rOut
endmodule

module rfile (
  input  globalReset,
  input  [2:0] rs1,
  input  [2:0] rs2,
  input  [2:0] rd,
  output [15:0] rs1val,
  output [15:0] rs2val
);

  Decoder decoder_1 ();  // open: out0, out1, sel, en
  register r0 (.rIn({16{1'b0}}), .Reset(globalReset));  // open: wEnable, rOut
  register r1 (.Reset(globalReset));  // open: rIn, wEnable, rOut
  register r2 (.Reset(globalReset));  // open: rIn, wEnable, rOut
  register r3 (.Reset(globalReset));  // open: rIn, wEnable, rOut
  register r4 (.Reset(globalReset));  // open: rIn, wEnable, rOut
  register r5 (.Reset(globalReset));  // open: rIn, wEnable, rOut
  register r6 (.Reset(globalReset));  // open: rIn, wEnable, rOut
  register r7 (.Reset(globalReset));  // open: rIn, wEnable, rOut
endmodule
