// Logisim project hw4.circ as structural Verilog
module register (
  input  [15:0] rIn,
  input  Reset,
  input  clock,
  input  wEnable,
  output [15:0] rOut
);

  wire [15:0] and_1_out, multiplexer_1_out, multiplexer_2_out;

  D_Flip_Flop d_ff_1 (.clk(clock), .D(multiplexer_2_out[15]), .Q(rOut[15]));  // open: Qn, preset, en, reset
  D_Flip_Flop d_ff_2 (.clk(clock), .D(multiplexer_2_out[14]), .Q(rOut[14]));  // open: Qn, preset, en, reset
  D_Flip_Flop d_ff_3 (.clk(clock), .D(multiplexer_2_out[13]), .Q(rOut[13]));  // open: Qn, preset, en, reset
  D_Flip_Flop d_ff_4 (.clk(clock), .D(multiplexer_2_out[12]), .Q(rOut[12]));  // open: Qn, preset, en, reset
  assign and_1_out = rIn & {16{1'b0}};  // AND_Gate and_1, 16 bits wide
  D_Flip_Flop d_ff_5 (.clk(clock), .D(multiplexer_2_out[11]), .Q(rOut[11]));  // open: Qn, preset, en, reset
  Multiplexer #(.width(16), .enable("false")) multiplexer_1 (
    .in0(rIn), .in1(and_1_out), .out(multiplexer_1_out), .sel(Reset));
  D_Flip_Flop d_ff_6 (.clk(clock), .D(multiplexer_2_out[10]), .Q(rOut[10]));  // open: Qn, preset, en, reset
  D_Flip_Flop d_ff_7 (.clk(clock), .D(multiplexer_2_out[9]), .Q(rOut[9]));  // open: Qn, preset, en, reset
  Multiplexer #(.width(16), .enable("false")) multiplexer_2 (
    .in0(rOut), .in1(multiplexer_1_out), .out(multiplexer_2_out), .sel(wEnable));
  D_Flip_Flop d_ff_8 (.clk(clock), .D(multiplexer_2_out[8]), .Q(rOut[8]));  // open: Qn, preset, en, reset
  D_Flip_Flop d_ff_9 (.clk(clock), .D(multiplexer_2_out[7]), .Q(rOut[7]));  // open: Qn, preset, en, reset
  D_Flip_Flop d_ff_10 (.clk(clock), .D(multiplexer_2_out[6]), .Q(rOut[6]));  // open: Qn, preset, en, reset
  D_Flip_Flop d_ff_11 (.clk(clock), .D(multiplexer_2_out[5]), .Q(rOut[5]));  // open: Qn, preset, en, reset
  D_Flip_Flop d_ff_12 (.clk(clock), .D(multiplexer_2_out[4]), .Q(rOut[4]));  // open: Qn, preset, en, reset
  D_Flip_Flop d_ff_13 (.clk(clock), .D(multiplexer_2_out[3]), .Q(rOut[3]));  // open: Qn, preset, en, reset
  D_Flip_Flop d_ff_14 (.clk(clock), .D(multiplexer_2_out[2]), .Q(rOut[2]));  // open: Qn, preset, en, reset
  D_Flip_Flop d_ff_15 (.clk(clock), .D(multiplexer_2_out[1]), .Q(rOut[1]));  // open: Qn, preset, en, reset
  D_Flip_Flop d_ff_16 (.clk(clock), .D(multiplexer_2_out[0]), .Q(rOut[0]));  // open: Qn, preset, en, reset

  // Other names for the same wires on the sheet: clk = clock; ot[15:0] = rOut
endmodule

module rfile (
  input  reset,
  input  clk,
  input  [15:0] WriteData,
  input  [2:0] ReadReg1,
  input  [2:0] ReadReg2,
  input  [2:0] rd,
  input  [2:0] WriteReg,
  output [15:0] ReadData1,
  output [15:0] ReadData2
);

  wire and_1_out, decoder_2_out0, decoder_2_out1, decoder_2_out2, decoder_2_out3, decoder_2_out4,
       decoder_2_out5, decoder_2_out6, decoder_2_out7, decoder_3_out0, decoder_3_out1, decoder_3_out2,
       decoder_3_out3, decoder_3_out4, decoder_3_out5, decoder_3_out6, decoder_3_out7, w0, w1, w2, w3, w4,
       w5, w6, w7;
  wire [15:0] five, four, one, sev, six, three, two, zero;

  assign ReadData2 = decoder_2_out0 ? zero : 16'bz;  // Controlled_Buffer controlled_buffer_1
  assign ReadData2 = decoder_2_out2 ? two : 16'bz;  // Controlled_Buffer controlled_buffer_2
  assign ReadData2 = decoder_2_out1 ? one : 16'bz;  // Controlled_Buffer controlled_buffer_3
  Decoder #(.select(3)) decoder_1 (
    .out0(w0), .out1(w1), .out2(w2), .out3(w3), .out4(w4), .out5(w5), .out6(w6), .out7(w7), .sel(WriteReg),
    .en(1'b1));
  assign ReadData2 = decoder_2_out5 ? two : 16'bz;  // Controlled_Buffer controlled_buffer_4
  assign ReadData2 = decoder_2_out4 ? one : 16'bz;  // Controlled_Buffer controlled_buffer_5
  assign ReadData2 = decoder_2_out3 ? zero : 16'bz;  // Controlled_Buffer controlled_buffer_6
  Decoder #(.select(3)) decoder_2 (
    .out0(decoder_2_out0), .out1(decoder_2_out1), .out2(decoder_2_out2), .out3(decoder_2_out3),
    .out4(decoder_2_out4), .out5(decoder_2_out5), .out6(decoder_2_out6), .out7(decoder_2_out7),
    .sel(ReadReg2), .en(1'b1));
  assign ReadData2 = decoder_2_out7 ? two : 16'bz;  // Controlled_Buffer controlled_buffer_7
  assign ReadData2 = decoder_2_out6 ? one : 16'bz;  // Controlled_Buffer controlled_buffer_8
  register r0 (.rIn({16{1'b0}}), .clock(clk), .Reset(reset), .wEnable(and_1_out), .rOut(zero));
  and and_1 (and_1_out, 1'b0, w0);
  register r1 (.rIn(WriteData), .clock(clk), .Reset(reset), .wEnable(w1), .rOut(one));
  // Probe on one
  register r2 (.rIn(WriteData), .clock(clk), .Reset(reset), .wEnable(w2), .rOut(two));
  register r3 (.rIn(WriteData), .clock(clk), .Reset(reset), .wEnable(w3), .rOut(three));
  register r4 (.rIn(WriteData), .clock(clk), .Reset(reset), .wEnable(w4), .rOut(four));
  register r5 (.rIn(WriteData), .clock(clk), .Reset(reset), .wEnable(w5), .rOut(five));
  assign ReadData1 = decoder_3_out2 ? two : 16'bz;  // Controlled_Buffer controlled_buffer_9
  assign ReadData1 = decoder_3_out1 ? one : 16'bz;  // Controlled_Buffer controlled_buffer_10
  assign ReadData1 = decoder_3_out0 ? zero : 16'bz;  // Controlled_Buffer controlled_buffer_11
  register r6 (.rIn(WriteData), .clock(clk), .Reset(reset), .wEnable(w6), .rOut(six));
  assign ReadData1 = decoder_3_out5 ? five : 16'bz;  // Controlled_Buffer controlled_buffer_12
  assign ReadData1 = decoder_3_out4 ? four : 16'bz;  // Controlled_Buffer controlled_buffer_13
  assign ReadData1 = decoder_3_out3 ? three : 16'bz;  // Controlled_Buffer controlled_buffer_14
  Decoder #(.select(3)) decoder_3 (
    .out0(decoder_3_out0), .out1(decoder_3_out1), .out2(decoder_3_out2), .out3(decoder_3_out3),
    .out4(decoder_3_out4), .out5(decoder_3_out5), .out6(decoder_3_out6), .out7(decoder_3_out7),
    .sel(ReadReg1), .en(1'b1));
  assign ReadData1 = decoder_3_out7 ? sev : 16'bz;  // Controlled_Buffer controlled_buffer_15
  assign ReadData1 = decoder_3_out6 ? six : 16'bz;  // Controlled_Buffer controlled_buffer_16
  register r7 (.rIn(WriteData), .clock(clk), .Reset(reset), .wEnable(w7), .rOut(sev));

  // Other names for the same wires on the sheet: clkT = clk; reg1Num[2:0] = ReadReg1; reg2Num[2:0] = ReadReg2;
  //   wvalT[15:0] = WriteData
endmodule

module add (
  input  cin,
  input  a,
  input  b,
  output sum,
  output carry
);

  wire and_1_out, and_2_out, xor_1_out;

  xor xor_1 (xor_1_out, a, b);
  and and_1 (and_1_out, b, a);
  and and_2 (and_2_out, cin, xor_1_out);
  xor xor_2 (sum, cin, xor_1_out);
  or or_1 (carry, and_2_out, and_1_out);

  // Notes on the sheet:
  //   carry
endmodule

module addsub (
  input  [15:0] A,
  input  [15:0] B,
  input  sub,
  output ovf,
  output [15:0] result
);

  wire add_1_carry, add_2_carry, add_3_carry, add_4_carry, add_5_carry, add_6_carry, add_7_carry,
       add_8_carry, add_9_carry, add_10_carry, add_11_carry, add_12_carry, add_13_carry, add_14_carry,
       add_15_carry, add_16_carry, multiplexer_2_out;
  wire [15:0] multiplexer_1_out, not_1_out;

  add add_1 (.cin(add_2_carry), .a(A[15]), .b(multiplexer_1_out[15]), .sum(result[15]), .carry(add_1_carry));
  xor xor_1 (ovf, add_2_carry, add_1_carry);
  add add_2 (.cin(add_3_carry), .a(A[14]), .b(multiplexer_1_out[14]), .sum(result[14]), .carry(add_2_carry));
  add add_3 (.cin(add_4_carry), .a(A[13]), .b(multiplexer_1_out[13]), .sum(result[13]), .carry(add_3_carry));
  assign not_1_out = ~B;  // NOT_Gate not_1, 16 bits wide
  add add_4 (.cin(add_5_carry), .a(A[12]), .b(multiplexer_1_out[12]), .sum(result[12]), .carry(add_4_carry));
  add add_5 (.cin(add_6_carry), .a(A[11]), .b(multiplexer_1_out[11]), .sum(result[11]), .carry(add_5_carry));
  Multiplexer #(.width(16)) multiplexer_1 (.in0(B), .in1(not_1_out), .out(multiplexer_1_out), .sel(sub));  // open: en
  add add_6 (.cin(add_7_carry), .a(A[10]), .b(multiplexer_1_out[10]), .sum(result[10]), .carry(add_6_carry));
  add add_7 (.cin(add_8_carry), .a(A[9]), .b(multiplexer_1_out[9]), .sum(result[9]), .carry(add_7_carry));
  add add_8 (.cin(add_9_carry), .a(A[8]), .b(multiplexer_1_out[8]), .sum(result[8]), .carry(add_8_carry));
  add add_9 (.cin(add_10_carry), .a(A[7]), .b(multiplexer_1_out[7]), .sum(result[7]), .carry(add_9_carry));
  add add_10 (.cin(add_11_carry), .a(A[6]), .b(multiplexer_1_out[6]), .sum(result[6]), .carry(add_10_carry));
  add add_11 (.cin(add_12_carry), .a(A[5]), .b(multiplexer_1_out[5]), .sum(result[5]), .carry(add_11_carry));
  add add_12 (.cin(add_13_carry), .a(A[4]), .b(multiplexer_1_out[4]), .sum(result[4]), .carry(add_12_carry));
  add add_13 (.cin(add_14_carry), .a(A[3]), .b(multiplexer_1_out[3]), .sum(result[3]), .carry(add_13_carry));
  add add_14 (.cin(add_15_carry), .a(A[2]), .b(multiplexer_1_out[2]), .sum(result[2]), .carry(add_14_carry));
  add add_15 (.cin(add_16_carry), .a(A[1]), .b(multiplexer_1_out[1]), .sum(result[1]), .carry(add_15_carry));
  add add_16 (.cin(multiplexer_2_out), .a(A[0]), .b(multiplexer_1_out[0]), .sum(result[0]), .carry(add_16_carry));
  Multiplexer multiplexer_2 (.in0(1'b0), .in1(1'b1), .out(multiplexer_2_out), .sel(sub));  // open: en
endmodule

module negator (
  input  [15:0] nIn,
  output [15:0] nOut
);

  assign nOut = ~nIn;  // NOT_Gate not_1, 16 bits wide
endmodule

module xorer (
  input  [15:0] xIn1,
  input  [15:0] xIn2,
  output [15:0] xOut
);

  assign xOut = xIn1 ^ xIn2;  // XOR_Gate xor_1, 16 bits wide
endmodule

module rshifter (
  input  [15:0] in,
  input  [2:0] shamt,
  output [15:0] out_3
);

  wire multiplexer_1_out, multiplexer_2_out, multiplexer_3_out, multiplexer_4_out, multiplexer_5_out,
       multiplexer_6_out, multiplexer_7_out, multiplexer_8_out, multiplexer_9_out, multiplexer_10_out,
       multiplexer_11_out, multiplexer_12_out, multiplexer_13_out, multiplexer_14_out, multiplexer_15_out,
       multiplexer_16_out, multiplexer_17_out, multiplexer_18_out, multiplexer_19_out, multiplexer_20_out,
       multiplexer_21_out, multiplexer_22_out, multiplexer_23_out, multiplexer_24_out, multiplexer_25_out,
       multiplexer_26_out, multiplexer_27_out, multiplexer_28_out, multiplexer_29_out, multiplexer_30_out,
       multiplexer_31_out, multiplexer_32_out;

  Multiplexer #(.enable("false")) multiplexer_1 (.in0(in[0]), .in1(in[1]), .out(multiplexer_1_out), .sel(shamt[0]));
  Multiplexer #(.enable("false")) multiplexer_2 (.in0(in[1]), .in1(in[2]), .out(multiplexer_2_out), .sel(shamt[0]));
  Multiplexer #(.enable("false")) multiplexer_3 (.in0(in[2]), .in1(in[3]), .out(multiplexer_3_out), .sel(shamt[0]));
  Multiplexer #(.enable("false")) multiplexer_4 (.in0(in[3]), .in1(in[4]), .out(multiplexer_4_out), .sel(shamt[0]));
  Multiplexer #(.enable("false")) multiplexer_5 (.in0(in[4]), .in1(in[5]), .out(multiplexer_5_out), .sel(shamt[0]));
  Multiplexer #(.enable("false")) multiplexer_6 (.in0(in[5]), .in1(in[6]), .out(multiplexer_6_out), .sel(shamt[0]));
  Multiplexer #(.enable("false")) multiplexer_7 (.in0(in[6]), .in1(in[7]), .out(multiplexer_7_out), .sel(shamt[0]));
  Multiplexer #(.enable("false")) multiplexer_8 (.in0(in[7]), .in1(in[8]), .out(multiplexer_8_out), .sel(shamt[0]));
  Multiplexer #(.enable("false")) multiplexer_9 (.in0(in[8]), .in1(in[9]), .out(multiplexer_9_out), .sel(shamt[0]));
  Multiplexer #(.enable("false")) multiplexer_10 (.in0(in[9]), .in1(in[10]), .out(multiplexer_10_out), .sel(shamt[0]));
  Multiplexer #(.enable("false")) multiplexer_11 (.in0(in[10]), .in1(in[11]), .out(multiplexer_11_out), .sel(shamt[0]));
  Multiplexer #(.enable("false")) multiplexer_12 (.in0(in[11]), .in1(in[12]), .out(multiplexer_12_out), .sel(shamt[0]));
  Multiplexer #(.enable("false")) multiplexer_13 (.in0(in[12]), .in1(in[13]), .out(multiplexer_13_out), .sel(shamt[0]));
  Multiplexer #(.enable("false")) multiplexer_14 (.in0(in[13]), .in1(in[14]), .out(multiplexer_14_out), .sel(shamt[0]));
  Multiplexer #(.enable("false")) multiplexer_15 (.in0(in[14]), .in1(in[15]), .out(multiplexer_15_out), .sel(shamt[0]));
  Multiplexer #(.enable("false")) multiplexer_16 (.in0(in[15]), .in1(in[15]), .out(multiplexer_16_out), .sel(shamt[0]));
  Multiplexer #(.enable("false")) multiplexer_17 (
    .in0(multiplexer_1_out), .in1(multiplexer_3_out), .out(multiplexer_17_out), .sel(shamt[1]));
  Multiplexer #(.enable("false")) multiplexer_18 (
    .in0(multiplexer_2_out), .in1(multiplexer_4_out), .out(multiplexer_18_out), .sel(shamt[1]));
  Multiplexer #(.enable("false")) multiplexer_19 (
    .in0(multiplexer_3_out), .in1(multiplexer_5_out), .out(multiplexer_19_out), .sel(shamt[1]));
  Multiplexer #(.enable("false")) multiplexer_20 (
    .in0(multiplexer_4_out), .in1(multiplexer_6_out), .out(multiplexer_20_out), .sel(shamt[1]));
  Multiplexer #(.enable("false")) multiplexer_21 (
    .in0(multiplexer_5_out), .in1(multiplexer_7_out), .out(multiplexer_21_out), .sel(shamt[1]));
  Multiplexer #(.enable("false")) multiplexer_22 (
    .in0(multiplexer_6_out), .in1(multiplexer_8_out), .out(multiplexer_22_out), .sel(shamt[1]));
  Multiplexer #(.enable("false")) multiplexer_23 (
    .in0(multiplexer_7_out), .in1(multiplexer_9_out), .out(multiplexer_23_out), .sel(shamt[1]));
  Multiplexer #(.enable("false")) multiplexer_24 (
    .in0(multiplexer_8_out), .in1(multiplexer_10_out), .out(multiplexer_24_out), .sel(shamt[1]));
  Multiplexer #(.enable("false")) multiplexer_25 (
    .in0(multiplexer_9_out), .in1(multiplexer_11_out), .out(multiplexer_25_out), .sel(shamt[1]));
  Multiplexer #(.enable("false")) multiplexer_26 (
    .in0(multiplexer_10_out), .in1(multiplexer_12_out), .out(multiplexer_26_out), .sel(shamt[1]));
  Multiplexer #(.enable("false")) multiplexer_27 (
    .in0(multiplexer_11_out), .in1(multiplexer_13_out), .out(multiplexer_27_out), .sel(shamt[1]));
  Multiplexer #(.enable("false")) multiplexer_28 (
    .in0(multiplexer_12_out), .in1(multiplexer_14_out), .out(multiplexer_28_out), .sel(shamt[1]));
  Multiplexer #(.enable("false")) multiplexer_29 (
    .in0(multiplexer_13_out), .in1(multiplexer_15_out), .out(multiplexer_29_out), .sel(shamt[1]));
  Multiplexer #(.enable("false")) multiplexer_30 (
    .in0(multiplexer_14_out), .in1(multiplexer_16_out), .out(multiplexer_30_out), .sel(shamt[1]));
  Multiplexer #(.enable("false")) multiplexer_31 (
    .in0(multiplexer_15_out), .in1(in[15]), .out(multiplexer_31_out), .sel(shamt[1]));
  Multiplexer #(.enable("false")) multiplexer_32 (
    .in0(multiplexer_16_out), .in1(in[15]), .out(multiplexer_32_out), .sel(shamt[1]));
  Multiplexer #(.enable("false")) multiplexer_33 (
    .in0(multiplexer_17_out), .in1(multiplexer_21_out), .out(out_3[0]), .sel(shamt[2]));
  Multiplexer #(.enable("false")) multiplexer_34 (
    .in0(multiplexer_18_out), .in1(multiplexer_22_out), .out(out_3[1]), .sel(shamt[2]));
  Multiplexer #(.enable("false")) multiplexer_35 (
    .in0(multiplexer_19_out), .in1(multiplexer_23_out), .out(out_3[2]), .sel(shamt[2]));
  Multiplexer #(.enable("false")) multiplexer_36 (
    .in0(multiplexer_20_out), .in1(multiplexer_24_out), .out(out_3[3]), .sel(shamt[2]));
  Multiplexer #(.enable("false")) multiplexer_37 (
    .in0(multiplexer_21_out), .in1(multiplexer_25_out), .out(out_3[4]), .sel(shamt[2]));
  Multiplexer #(.enable("false")) multiplexer_38 (
    .in0(multiplexer_22_out), .in1(multiplexer_26_out), .out(out_3[5]), .sel(shamt[2]));
  Multiplexer #(.enable("false")) multiplexer_39 (
    .in0(multiplexer_26_out), .in1(multiplexer_27_out), .out(out_3[6]), .sel(shamt[2]));
  Multiplexer #(.enable("false")) multiplexer_40 (
    .in0(multiplexer_24_out), .in1(multiplexer_28_out), .out(out_3[7]), .sel(shamt[2]));
  Multiplexer #(.enable("false")) multiplexer_41 (
    .in0(multiplexer_25_out), .in1(multiplexer_29_out), .out(out_3[8]), .sel(shamt[2]));
  Multiplexer #(.enable("false")) multiplexer_42 (
    .in0(multiplexer_26_out), .in1(multiplexer_30_out), .out(out_3[9]), .sel(shamt[2]));
  Multiplexer #(.enable("false")) multiplexer_43 (
    .in0(multiplexer_27_out), .in1(multiplexer_31_out), .out(out_3[10]), .sel(shamt[2]));
  Multiplexer #(.enable("false")) multiplexer_44 (
    .in0(multiplexer_28_out), .in1(multiplexer_32_out), .out(out_3[11]), .sel(shamt[2]));
  Multiplexer #(.enable("false")) multiplexer_45 (
    .in0(multiplexer_29_out), .in1(in[15]), .out(out_3[12]), .sel(shamt[2]));
  Multiplexer #(.enable("false")) multiplexer_46 (
    .in0(multiplexer_30_out), .in1(in[15]), .out(out_3[13]), .sel(shamt[2]));
  Multiplexer #(.enable("false")) multiplexer_47 (
    .in0(multiplexer_31_out), .in1(in[15]), .out(out_3[14]), .sel(shamt[2]));
  Multiplexer #(.enable("false")) multiplexer_48 (
    .in0(multiplexer_32_out), .in1(in[15]), .out(out_3[15]), .sel(shamt[2]));

  // Other names for the same wires on the sheet: _0 = in[0]; _1 = in[1]; _2 = in[2]; _3 = in[3]; _4 = in[4];
  //   _5 = in[5]; _6 = in[6]; _7 = in[7]; _8 = in[8]; _9 = in[9]; _10 = in[10]; _11 = in[11]; _12 = in[12];
  //   _13 = in[13]; _14 = in[14]; _15 = in[15]; s0 = shamt[0]; s1 = shamt[1]; s2 = shamt[2]
endmodule

module ALU (
  input  [2:0] shAmt,
  input  [15:0] InputData1,
  input  [15:0] InputData2,
  input  [3:0] OpCode,
  output [15:0] out_5
);

  wire decoder_1_out0, decoder_1_out1, decoder_1_out2, decoder_1_out3, decoder_1_out4, decoder_1_out5,
       decoder_1_out6;
  wire [15:0] addout, lsout, nOut, rsout, subout, xorout;

  addsub addsub_1 (.result(addout), .sub(1'b0), .A(InputData1), .B(InputData2));  // open: ovf
  lshifter lshifter_1 (.in(InputData1), .shamt(shAmt), .out(lsout));
  negator negator_1 (.nIn(InputData1), .nOut(nOut));
  addsub addsub_2 (.result(subout), .sub(1'b1), .A(InputData1), .B(InputData2));  // open: ovf
  rshifter rshifter_1 (.in(InputData1), .shamt(shAmt), .out_3(rsout));
  xorer xorer_1 (.xIn1(InputData1), .xIn2(InputData2), .xOut(xorout));
  assign out_5 = decoder_1_out6 ? rsout : 16'bz;  // Controlled_Buffer controlled_buffer_1
  assign out_5 = decoder_1_out5 ? lsout : 16'bz;  // Controlled_Buffer controlled_buffer_2
  assign out_5 = decoder_1_out4 ? xorout : 16'bz;  // Controlled_Buffer controlled_buffer_3
  assign out_5 = decoder_1_out3 ? nOut : 16'bz;  // Controlled_Buffer controlled_buffer_4
  assign out_5 = decoder_1_out2 ? subout : 16'bz;  // Controlled_Buffer controlled_buffer_5
  assign out_5 = decoder_1_out1 ? addout : 16'bz;  // Controlled_Buffer controlled_buffer_6
  assign out_5 = decoder_1_out0 ? addout : 16'bz;  // Controlled_Buffer controlled_buffer_7
  Decoder #(.select(4)) decoder_1 (
    .out0(decoder_1_out0), .out1(decoder_1_out1), .out2(decoder_1_out2), .out3(decoder_1_out3),
    .out4(decoder_1_out4), .out5(decoder_1_out5), .out6(decoder_1_out6), .sel(OpCode), .en(1'b1));  // open: out7, out8, out9, out10, out11, out12, out13, out14, out15

  // Other names for the same wires on the sheet: in1[15:0] = InputData1; in2[15:0] = InputData2; sh[2:0] = shAmt
endmodule

module lshifter (
  input  [15:0] in,
  input  [2:0] shamt,
  output [15:0] out
);

  wire multiplexer_1_out, multiplexer_2_out, multiplexer_3_out, multiplexer_4_out, multiplexer_5_out,
       multiplexer_6_out, multiplexer_7_out, multiplexer_8_out, multiplexer_9_out, multiplexer_10_out,
       multiplexer_11_out, multiplexer_12_out, multiplexer_13_out, multiplexer_14_out, multiplexer_15_out,
       multiplexer_16_out, multiplexer_17_out, multiplexer_18_out, multiplexer_19_out, multiplexer_20_out,
       multiplexer_21_out, multiplexer_22_out, multiplexer_23_out, multiplexer_24_out, multiplexer_25_out,
       multiplexer_26_out, multiplexer_27_out, multiplexer_28_out, multiplexer_29_out, multiplexer_30_out,
       multiplexer_31_out, multiplexer_32_out;

  Multiplexer #(.enable("false")) multiplexer_1 (.in0(in[0]), .in1(1'b0), .out(multiplexer_1_out), .sel(shamt[0]));
  Multiplexer #(.enable("false")) multiplexer_2 (.in0(in[1]), .in1(in[0]), .out(multiplexer_2_out), .sel(shamt[0]));
  Multiplexer #(.enable("false")) multiplexer_3 (.in0(in[2]), .in1(in[1]), .out(multiplexer_3_out), .sel(shamt[0]));
  Multiplexer #(.enable("false")) multiplexer_4 (.in0(in[3]), .in1(in[2]), .out(multiplexer_4_out), .sel(shamt[0]));
  Multiplexer #(.enable("false")) multiplexer_5 (.in0(in[4]), .in1(in[3]), .out(multiplexer_5_out), .sel(shamt[0]));
  Multiplexer #(.enable("false")) multiplexer_6 (.in0(in[5]), .in1(in[4]), .out(multiplexer_6_out), .sel(shamt[0]));
  Multiplexer #(.enable("false")) multiplexer_7 (.in0(in[6]), .in1(in[5]), .out(multiplexer_7_out), .sel(shamt[0]));
  Multiplexer #(.enable("false")) multiplexer_8 (.in0(in[7]), .in1(in[6]), .out(multiplexer_8_out), .sel(shamt[0]));
  Multiplexer #(.enable("false")) multiplexer_9 (.in0(in[8]), .in1(in[7]), .out(multiplexer_9_out), .sel(shamt[0]));
  Multiplexer #(.enable("false")) multiplexer_10 (.in0(in[9]), .in1(in[8]), .out(multiplexer_10_out), .sel(shamt[0]));
  Multiplexer #(.enable("false")) multiplexer_11 (.in0(in[10]), .in1(in[9]), .out(multiplexer_11_out), .sel(shamt[0]));
  Multiplexer #(.enable("false")) multiplexer_12 (.in0(in[11]), .in1(in[10]), .out(multiplexer_12_out), .sel(shamt[0]));
  Multiplexer #(.enable("false")) multiplexer_13 (.in0(in[12]), .in1(in[11]), .out(multiplexer_13_out), .sel(shamt[0]));
  Multiplexer #(.enable("false")) multiplexer_14 (.in0(in[13]), .in1(in[12]), .out(multiplexer_14_out), .sel(shamt[0]));
  Multiplexer #(.enable("false")) multiplexer_15 (.in0(in[14]), .in1(in[13]), .out(multiplexer_15_out), .sel(shamt[0]));
  Multiplexer #(.enable("false")) multiplexer_16 (.in0(in[15]), .in1(in[14]), .out(multiplexer_16_out), .sel(shamt[0]));
  Multiplexer #(.enable("false")) multiplexer_17 (
    .in0(multiplexer_1_out), .in1(1'b0), .out(multiplexer_17_out), .sel(shamt[1]));
  Multiplexer #(.enable("false")) multiplexer_18 (
    .in0(multiplexer_2_out), .in1(1'b0), .out(multiplexer_18_out), .sel(shamt[1]));
  Multiplexer #(.enable("false")) multiplexer_19 (
    .in0(multiplexer_3_out), .in1(multiplexer_1_out), .out(multiplexer_19_out), .sel(shamt[1]));
  Multiplexer #(.enable("false")) multiplexer_20 (
    .in0(multiplexer_4_out), .in1(multiplexer_2_out), .out(multiplexer_20_out), .sel(shamt[1]));
  Multiplexer #(.enable("false")) multiplexer_21 (
    .in0(multiplexer_5_out), .in1(multiplexer_3_out), .out(multiplexer_21_out), .sel(shamt[1]));
  Multiplexer #(.enable("false")) multiplexer_22 (
    .in0(multiplexer_6_out), .in1(multiplexer_4_out), .out(multiplexer_22_out), .sel(shamt[1]));
  Multiplexer #(.enable("false")) multiplexer_23 (
    .in0(multiplexer_7_out), .in1(multiplexer_5_out), .out(multiplexer_23_out), .sel(shamt[1]));
  Multiplexer #(.enable("false")) multiplexer_24 (
    .in0(multiplexer_8_out), .in1(multiplexer_6_out), .out(multiplexer_24_out), .sel(shamt[1]));
  Multiplexer #(.enable("false")) multiplexer_25 (
    .in0(multiplexer_9_out), .in1(multiplexer_7_out), .out(multiplexer_25_out), .sel(shamt[1]));
  Multiplexer #(.enable("false")) multiplexer_26 (
    .in0(multiplexer_10_out), .in1(multiplexer_8_out), .out(multiplexer_26_out), .sel(shamt[1]));
  Multiplexer #(.enable("false")) multiplexer_27 (
    .in0(multiplexer_11_out), .in1(multiplexer_9_out), .out(multiplexer_27_out), .sel(shamt[1]));
  Multiplexer #(.enable("false")) multiplexer_28 (
    .in0(multiplexer_12_out), .in1(multiplexer_10_out), .out(multiplexer_28_out), .sel(shamt[1]));
  Multiplexer #(.enable("false")) multiplexer_29 (
    .in0(multiplexer_13_out), .in1(multiplexer_11_out), .out(multiplexer_29_out), .sel(shamt[1]));
  Multiplexer #(.enable("false")) multiplexer_30 (
    .in0(multiplexer_14_out), .in1(multiplexer_12_out), .out(multiplexer_30_out), .sel(shamt[1]));
  Multiplexer #(.enable("false")) multiplexer_31 (
    .in0(multiplexer_15_out), .in1(multiplexer_13_out), .out(multiplexer_31_out), .sel(shamt[1]));
  Multiplexer #(.enable("false")) multiplexer_32 (
    .in0(multiplexer_16_out), .in1(multiplexer_14_out), .out(multiplexer_32_out), .sel(shamt[1]));
  Multiplexer #(.enable("false")) multiplexer_33 (.in0(multiplexer_17_out), .in1(1'b0), .out(out[0]), .sel(shamt[2]));
  Multiplexer #(.enable("false")) multiplexer_34 (.in0(multiplexer_18_out), .in1(1'b0), .out(out[1]), .sel(shamt[2]));
  Multiplexer #(.enable("false")) multiplexer_35 (.in0(multiplexer_19_out), .in1(1'b0), .out(out[2]), .sel(shamt[2]));
  Multiplexer #(.enable("false")) multiplexer_36 (.in0(multiplexer_20_out), .in1(1'b0), .out(out[3]), .sel(shamt[2]));
  Multiplexer #(.enable("false")) multiplexer_37 (
    .in0(multiplexer_21_out), .in1(multiplexer_17_out), .out(out[4]), .sel(shamt[2]));
  Multiplexer #(.enable("false")) multiplexer_38 (
    .in0(multiplexer_22_out), .in1(multiplexer_18_out), .out(out[5]), .sel(shamt[2]));
  Multiplexer #(.enable("false")) multiplexer_39 (
    .in0(multiplexer_23_out), .in1(multiplexer_19_out), .out(out[6]), .sel(shamt[2]));
  Multiplexer #(.enable("false")) multiplexer_40 (
    .in0(multiplexer_24_out), .in1(multiplexer_20_out), .out(out[7]), .sel(shamt[2]));
  Multiplexer #(.enable("false")) multiplexer_41 (
    .in0(multiplexer_25_out), .in1(multiplexer_21_out), .out(out[8]), .sel(shamt[2]));
  Multiplexer #(.enable("false")) multiplexer_42 (
    .in0(multiplexer_26_out), .in1(multiplexer_22_out), .out(out[9]), .sel(shamt[2]));
  Multiplexer #(.enable("false")) multiplexer_43 (
    .in0(multiplexer_27_out), .in1(multiplexer_23_out), .out(out[10]), .sel(shamt[2]));
  Multiplexer #(.enable("false")) multiplexer_44 (
    .in0(multiplexer_28_out), .in1(multiplexer_24_out), .out(out[11]), .sel(shamt[2]));
  Multiplexer #(.enable("false")) multiplexer_45 (
    .in0(multiplexer_29_out), .in1(multiplexer_25_out), .out(out[12]), .sel(shamt[2]));
  Multiplexer #(.enable("false")) multiplexer_46 (
    .in0(multiplexer_30_out), .in1(multiplexer_26_out), .out(out[13]), .sel(shamt[2]));
  Multiplexer #(.enable("false")) multiplexer_47 (
    .in0(multiplexer_31_out), .in1(multiplexer_27_out), .out(out[14]), .sel(shamt[2]));
  Multiplexer #(.enable("false")) multiplexer_48 (
    .in0(multiplexer_32_out), .in1(multiplexer_28_out), .out(out[15]), .sel(shamt[2]));

  // Other names for the same wires on the sheet: _0 = in[0]; _1 = in[1]; _2 = in[2]; _3 = in[3]; _4 = in[4];
  //   _5 = in[5]; _6 = in[6]; _7 = in[7]; _8 = in[8]; _9 = in[9]; _10 = in[10]; _11 = in[11]; _12 = in[12];
  //   _13 = in[13]; _14 = in[14]; _15 = in[15]; s0 = shamt[0]; s1 = shamt[1]; s2 = shamt[2]
endmodule
